# Fritzing sketch Controller-Schematic-Rev_A.1 (saved by Fritzing 0.9.10b)
breadboards: 4

parts:
  U1 = 4070 4 x 2 Input XOR Gate, single part [part_number=4070 package="DIP (Dual Inline) [THT]"]
  U2 = 4081 4 x 2 Input AND Gate, multi-part [part_number=4081 package="DIP (Dual Inline) [THT]"]
  Part2 = 4081_4_x_2_input_AND_gate_multipart_subpart1 [part_number=4081]  # not connected
  U2_1 = 4081_4_x_2_input_AND_gate_multipart_subpart2 [part_number=4081]  # not connected
  U2_3 = 4081_4_x_2_input_AND_gate_multipart_subpart4 [part_number=4081]  # not connected
  U3 = 74HC595 [package="DIP16 [THT]"]
  U4 = 74HC595 [package="DIP16 [THT]"]
  U5 = 74HC595 [package="DIP16 [THT]"]
  FUEL = IC, DIP package, 8 pins [chip_label=LTC1690]
  OX = IC, DIP package, 8 pins [chip_label=LTC1690]
  C3 = Electrolytic Capacitor [capacitance=100nF voltage=100V part_number=UVR2A0R1MDD1TD package="100 mil [THT, electrolytic]"]
  C4 = Electrolytic Capacitor [capacitance=1µF voltage=50V part_number=50YXF1MEFCT15X11 package="100 mil [THT, electrolytic]"]
  LM1084-3_3V = Voltage Regulator - 3.3V [part_number=LM1084IT-3.3/NOPB package="TO220 [THT]"]
  C1 = Electrolytic Capacitor [capacitance=10µF voltage=16V part_number=ECA-1CM100I package="100 mil [THT, electrolytic]"]
  C5 = Electrolytic Capacitor [capacitance=100nF voltage=100V part_number=UVR2A0R1MDD1TD package="100 mil [THT, electrolytic]"]
  C6 = Electrolytic Capacitor [capacitance=1µF voltage=50V part_number=50YXF1MEFCT15X11 package="100 mil [THT, electrolytic]"]
  C7 = Electrolytic Capacitor [capacitance=100nF voltage=100V part_number=UVR2A0R1MDD1TD package="100 mil [THT, electrolytic]"]
  C8 = Electrolytic Capacitor [capacitance=1µF voltage=50V part_number=50YXF1MEFCT15X11 package="100 mil [THT, electrolytic]"]
  C2 = Tantalum Capacitor [capacitance=10µF voltage=10V package="200 mil [THT, tantalum]"]
  C9 = Electrolytic Capacitor [capacitance=100nF voltage=100V part_number=UVR2A0R1MDD1TD package="100 mil [THT, electrolytic]"]
  C10 = Electrolytic Capacitor [capacitance=100nF voltage=100V part_number=UVR2A0R1MDD1TD package="100 mil [THT, electrolytic]"]
  TPQ1 = DIP - 14 pins [chip_label=TPQ3906 package="DIP (Dual Inline) [THT]"]
  J1 = Screw terminal - 2 pins [package=THT]
  Part3 = Arduino Nano 33 IOT
  R1 = Resistor [tolerance=±5% power=0.25 resistance=4.7k package=THT]
  R2 = Resistor [tolerance=±5% power=0.25 resistance=4.7k package=THT]
  R3 = Resistor [tolerance=±5% power=0.25 resistance=4.7k package=THT]
  R4 = Resistor [tolerance=±5% power=0.25 resistance=4.7k package=THT]
  J4 = male pin header, 8 pins [form="♂ (male)"]
  J3 = male pin header, 8 pins [form="♂ (male)"]
  J2 = male pin header, 8 pins [form="♂ (male)"]
  FUEL_2 = DB9 Connector [package=db9]
  OX_2 = DB9 Connector [package=db9]
  << = Pushbutton [package="[THT]"]
  >> = Pushbutton [package="[THT]"]
  S1 = Toggle Switch [package=THT]
  R5 = Resistor [tolerance=±5% power=0.25 resistance=4.7k package=THT]
  TPQ2 = DIP - 14 pins [chip_label=TPQ3906 package="DIP (Dual Inline) [THT]"]
  R7 = Resistor [tolerance=±5% power=0.25 resistance=4.7k package=THT]
  R8 = Resistor [tolerance=±5% power=0.25 resistance=4.7k package=THT]
  R9 = Resistor [tolerance=±5% power=0.25 resistance=4.7k package=THT]
  R6 = Resistor [tolerance=±5% power=0.25 resistance=4.7k package=THT]
  R10 = Resistor [tolerance=±5% resistance=1k power=0.25 package="0402 [SMD]"]
  R11 = Resistor [tolerance=±5% resistance=1k power=0.25 package="0402 [SMD]"]
  R12 = Resistor [tolerance=±5% resistance=1k power=0.25 package="0402 [SMD]"]
  R13 = Resistor [tolerance=±5% resistance=1k power=0.25 package="0402 [SMD]"]
  R14 = Resistor [tolerance=±5% resistance=1k power=0.25 package="0402 [SMD]"]
  R15 = Resistor [tolerance=±5% resistance=1k power=0.25 package="0402 [SMD]"]
  R16 = Resistor [tolerance=±5% resistance=1k power=0.25 package="0402 [SMD]"]
  R17 = Resistor [tolerance=±5% resistance=1k power=0.25 package="0402 [SMD]"]
  R18 = Resistor [tolerance=±5% resistance=1k power=0.25 package="0402 [SMD]"]
  R19 = Resistor [tolerance=±5% resistance=1k power=0.25 package="0402 [SMD]"]
  R20 = Resistor [tolerance=±5% resistance=1k power=0.25 package="0402 [SMD]"]
  R21 = Resistor [tolerance=±5% resistance=1k power=0.25 package="0402 [SMD]"]
  R22 = Resistor [tolerance=±5% resistance=1k power=0.25 package="0402 [SMD]"]
  R23 = Resistor [tolerance=±5% resistance=1k power=0.25 package="0402 [SMD]"]
  R24 = Resistor [tolerance=±5% resistance=1k power=0.25 package="0402 [SMD]"]
  R25 = Resistor [tolerance=±5% resistance=1k power=0.25 package="0402 [SMD]"]
  R26 = Resistor [tolerance=±5% resistance=1k power=0.25 package="0402 [SMD]"]
  R27 = Resistor [tolerance=±5% resistance=1k power=0.25 package="0402 [SMD]"]

nets:
  N1: U1.A1, U1.B3, U2.connector0, U2.connector8, TPQ1.E1
  N2: U1.B1, U2.connector1, U3.SH_CP, U4.SH_CP, U5.SH_CP, TPQ1.E2
  N3: U1.Q1, OX.pin3
  GND: U1.GND, U2.connector6, U3.GND, U3.OE, U4.GND, U4.OE, U5.GND, U5.OE, FUEL.pin4, OX.pin4, C3.-, C4.-, LM1084-3_3V.GND, C1.-, C5.-, C6.-, C7.-, C8.-, C2.-, C9.-, J1.pin1, Part3.GND, Part3.D13~, R1.Pin_0, R2.Pin_0, R3.Pin_1, R4.Pin_1, <<.Pin_1, <<.Pin_2, >>.Pin_1, >>.Pin_2, R5.Pin_0, R7.Pin_1, R6.Pin_1
  N4: U1.A3, OX.pin2
  N5: U1.Q3, U2.connector9, U3.DS
  VCC: U1.VDD, U2.connector13, U3.MR, U3.VCC, U4.MR, U4.VCC, U5.MR, U5.VCC, FUEL.pin1, OX.pin1, C3.+, C4.+, LM1084-3_3V.input_voltage, C1.+, C5.+, C6.+, C7.+, C8.+, C9.+, C10.+, TPQ1.C1, TPQ1.C2, TPQ1.C3, J1.pin2, Part3.VIN, TPQ2.C1, TPQ2.C2, TPQ2.C3, TPQ2.C4, R8.Pin_0, R9.Pin_0
  N6: U2.connector2, FUEL.pin3
  N7: U2.connector7, FUEL.pin2
  N8: U3.Q1, J2.pin2
  N9: U3.Q2, J2.pin3
  N10: U3.Q3, J2.pin4
  N11: U3.Q4, J2.pin5
  N12: U3.Q5, J2.pin6
  N13: U3.Q6, J2.pin7
  N14: U3.Q7, J2.pin8
  N15: U3.Q7', U4.DS
  N16: U3.ST_CP, U4.ST_CP, U5.ST_CP, TPQ1.E3
  N17: U3.Q0, J2.pin1
  N18: U4.Q1, J3.pin2
  N19: U4.Q2, J3.pin3
  N20: U4.Q3, J3.pin4
  N21: U4.Q4, J3.pin5
  N22: U4.Q5, J3.pin6
  N23: U4.Q6, J3.pin7
  N24: U4.Q7, J3.pin8
  N25: U4.Q7', U5.DS
  N26: U4.Q0, J3.pin1
  N27: U5.Q1, J4.pin2
  N28: U5.Q2, J4.pin3
  N29: U5.Q3, J4.pin4
  N30: U5.Q4, J4.pin5
  N31: U5.Q5, J4.pin6
  N32: U5.Q6, J4.pin7
  N33: U5.Q7, J4.pin8
  N34: U5.Q7', TPQ1.B4, R1.Pin_1
  N35: U5.Q0, J4.pin1
  N36: FUEL.pin5, FUEL_2.4
  N37: FUEL.pin6, FUEL_2.3
  N38: FUEL.pin7, FUEL_2.2
  N39: FUEL.pin8, FUEL_2.1
  N40: OX.pin5, OX_2.4
  N41: OX.pin6, OX_2.3
  N42: OX.pin7, OX_2.2
  N43: OX.pin8, OX_2.1
  N44: LM1084-3_3V.output_voltage, C2.+, TPQ1.C4, S1.L1
  N45: TPQ1.B1, Part3.D2, R3.Pin_0
  N46: TPQ1.B2, Part3.D9~, R4.Pin_0
  N47: TPQ1.B3, Part3.D10~, R2.Pin_1
  N48: TPQ1.E4, Part3.TX
  N49: Part3.RESET, Part3.A7, R10.Pin_0, R11.Pin_0, R12.Pin_0
  N50: Part3.D3~, TPQ2.B1, R7.Pin_0
  N51: Part3.D4, S1.COM, R5.Pin_1
  N52: Part3.D5~, TPQ2.B4, R8.Pin_1
  N53: Part3.D6~, TPQ2.B2, R6.Pin_0
  N54: Part3.D7, TPQ2.B3, R9.Pin_1
  N55: Part3.D11/MOSI, Part3.+5V
  N56: Part3.A6, R13.Pin_0, R14.Pin_0, R15.Pin_0
  N57: Part3.A5, >>.Pin_3, >>.Pin_4
  N58: Part3.A4, <<.Pin_3, <<.Pin_4
  N59: Part3.A3, R16.Pin_0, R17.Pin_0, R18.Pin_0
  N60: Part3.A2, R19.Pin_0, R20.Pin_0, R21.Pin_0
  N61: Part3.A1, R22.Pin_0, R23.Pin_0, R24.Pin_0
  N62: Part3.A0, R25.Pin_0, R26.Pin_0, R27.Pin_0
  N63: FUEL_2.5, TPQ2.E2
  N64: FUEL_2.6, TPQ2.E1
  N65: FUEL_2.7, R19.Pin_1, R20.Pin_1, R21.Pin_1
  N66: FUEL_2.8, R22.Pin_1, R23.Pin_1, R24.Pin_1
  N67: FUEL_2.9, R25.Pin_1, R26.Pin_1, R27.Pin_1
  N68: OX_2.5, TPQ2.E3
  N69: OX_2.6, TPQ2.E4
  N70: OX_2.7, R10.Pin_1, R11.Pin_1, R12.Pin_1
  N71: OX_2.8, R13.Pin_1, R14.Pin_1, R15.Pin_1
  N72: OX_2.9, R16.Pin_1, R17.Pin_1, R18.Pin_1

custom parts:
  DIP - 14 pins: PNP Array
  Arduino Nano 33 IOT: The Arduino Nano 33 IoT is the easiest and cheapest point of entry to enhance existing devices (and creating new ones) to be part of the IoT and designing pico-network applications. Whether you are looking at building a sensor network connected to your office or home router, or if you want to create a BLE device sending data to a cellphone, the Nano 33 IoT is your one-stop-solution for many of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
