# Fritzing sketch Controller-Schematic-Rev_B (saved by Fritzing 0.9.10b)
breadboards: 3

parts:
  FUEL = IC, DIP package, 8 pins [chip_label=LTC1690]
  OX = IC, DIP package, 8 pins [chip_label=LTC1690]
  LM1084-3_3V = Voltage Regulator - 3.3V [part_number=LM1084IT-3.3/NOPB package="TO220 [THT]"]
  C1 = Electrolytic Capacitor [capacitance=10µF voltage=16V part_number=ECA-1CM100I package="100 mil [THT, electrolytic]"]
  C2 = Tantalum Capacitor [capacitance=10µF voltage=10V package="200 mil [THT, tantalum]"]
  TPQ1 = DIP - 14 pins [chip_label=TPQ3906 package="DIP (Dual Inline) [THT]"]
  POWER_IN = Screw terminal - 2 pins [package=THT]
  Part3 = Arduino Nano 33 IOT
  R1 = Resistor [tolerance=±5% power=0.25 resistance=4.7k package=THT]
  R3 = Resistor [tolerance=±5% power=0.25 resistance=4.7k package=THT]
  << = Pushbutton [package="[THT]"]
  >> = Pushbutton [package="[THT]"]
  S1 = Toggle Switch [package=THT]
  R5 = Resistor [tolerance=±5% power=0.25 resistance=4.7k package=THT]
  TPQ2 = DIP - 14 pins [chip_label=TPQ3906 package="DIP (Dual Inline) [THT]"]
  R7 = Resistor [tolerance=±5% power=0.25 resistance=4.7k package=THT]
  R8 = Resistor [tolerance=±5% power=0.25 resistance=4.7k package=THT]
  R9 = Resistor [tolerance=±5% power=0.25 resistance=4.7k package=THT]
  R6 = Resistor [tolerance=±5% power=0.25 resistance=4.7k package=THT]
  R4 = Resistor [tolerance=±5% power=0.25 resistance=4.7k package=THT]
  R2 = Resistor [tolerance=±5% power=0.25 resistance=4.7k package=THT]
  R11 = Resistor [tolerance=±5% power=0.25 resistance=4.7k package=THT]
  R10 = Resistor [tolerance=±5% power=0.25 resistance=4.7k package=THT]
  R14 = Resistor [tolerance=±5% power=0.25 resistance=4.7k package=THT]
  R15 = Resistor [tolerance=±5% power=0.25 resistance=4.7k package=THT]
  R16 = Resistor [tolerance=±5% power=0.25 resistance=4.7k package=THT]
  LC_I2C = Screw terminal - 2 pins [package=THT]
  R18 = Resistor [tolerance=±5% power=0.25 resistance=4.7k package=THT]
  >>_2 = male pin header, 2 pins [form="♂ (male)"]
  <<_2 = male pin header, 2 pins [form="♂ (male)"]
  R23 = Resistor [tolerance=±5% power=0.25 resistance=4.7k package=THT]
  R24 = Resistor [tolerance=±5% power=0.25 resistance=4.7k package=THT]
  LED1 = LED - 5mm [color="Red (633nm)" current=0.030 package="5 mm [THT]"]
  LED2 = LED - 5mm [color="Red (633nm)" current=0.030 package="5 mm [THT]"]
  LED3 = LED - 5mm [color="Red (633nm)" current=0.030 package="5 mm [THT]"]
  LED4 = LED - 5mm [color="Red (633nm)" current=0.030 package="5 mm [THT]"]
  LED5 = LED - 5mm [color="Red (633nm)" current=0.030 package="5 mm [THT]"]
  LED6 = LED - 5mm [color="Red (633nm)" current=0.030 package="5 mm [THT]"]
  LED7 = LED - 5mm [color="Red (633nm)" current=0.030 package="5 mm [THT]"]
  LED8 = LED - 5mm [color="Red (633nm)" current=30mA package="5 mm [THT]"]
  U3 = 74HC595 [package="DIP16 [THT]"]
  R25 = Resistor [tolerance=±5% power=0.25 resistance=470 package=THT]
  R26 = Resistor [tolerance=±5% power=0.25 resistance=470 package=THT]
  R27 = Resistor [tolerance=±5% power=0.25 resistance=470 package=THT]
  R28 = Resistor [tolerance=±5% power=0.25 resistance=470 package=THT]
  R29 = Resistor [tolerance=±5% power=0.25 resistance=470 package=THT]
  R30 = Resistor [tolerance=±5% power=0.25 resistance=470 package=THT]
  R31 = Resistor [tolerance=±5% power=0.25 resistance=470 package=THT]
  R32 = Resistor [tolerance=±5% power=0.25 resistance=470 package=THT]
  SELECT = male pin header, 3 pins [form="♂ (male)"]
  FUEL_2 = male pin header, 8 pins [form="♂ (male)"]
  OX_2 = male pin header, 8 pins [form="♂ (male)"]
  R33 = Resistor [tolerance=±5% power=0.25 resistance=4.7k package=THT]
  FUEL_SAFE = male pin header, 2 pins [form="♂ (male)"]
  OX_SAFE = male pin header, 2 pins [form="♂ (male)"]

nets:
  VIN: FUEL.pin1, OX.pin1, LM1084-3_3V.input_voltage, LM1084-3_3V.output_voltage, C1.+, C2.+, TPQ1.C1, TPQ1.C2, TPQ1.C3, TPQ1.C4, POWER_IN.pin2, Part3.VIN, S1.COM, TPQ2.C1, TPQ2.C2, TPQ2.C3, TPQ2.C4, R11.Pin_0, R10.Pin_0, R23.Pin_0, R24.Pin_0, U3.MR, U3.VCC, SELECT.pin2
  N1: FUEL.pin2, TPQ1.B4, R1.Pin_0
  N2: FUEL.pin3, TPQ1.E1, R3.Pin_0
  GND: FUEL.pin4, OX.pin4, LM1084-3_3V.GND, C1.-, C2.-, POWER_IN.pin1, Part3.GND, Part3.D13~, R1.Pin_1, R3.Pin_1, <<.Pin_1, <<.Pin_2, >>.Pin_1, >>.Pin_2, R5.Pin_0, R7.Pin_1, R8.Pin_0, R9.Pin_0, R6.Pin_1, R4.Pin_1, R2.Pin_1, R14.Pin_1, R15.Pin_1, R16.Pin_0, R18.Pin_1, >>_2.pin2, <<_2.pin2, U3.GND, U3.OE, U3.DS, R25.Pin_1, R26.Pin_1, R27.Pin_1, R28.Pin_1, R29.Pin_1, R30.Pin_1, R31.Pin_1, R32.Pin_1, FUEL_2.pin5, OX_2.pin5, R33.Pin_1
  N3: FUEL.pin5, FUEL_2.pin4
  N4: FUEL.pin6, FUEL_2.pin3
  N5: FUEL.pin7, FUEL_2.pin2
  N6: FUEL.pin8, FUEL_2.pin1
  N7: OX.pin2, TPQ1.B3, R4.Pin_0
  N8: OX.pin3, TPQ1.E2, R2.Pin_0
  N9: OX.pin5, OX_2.pin4
  N10: OX.pin6, OX_2.pin3
  N11: OX.pin7, OX_2.pin2
  N12: OX.pin8, OX_2.pin1
  N13: TPQ1.B1, Part3.D11/MOSI, Part3.+5V, R10.Pin_1
  N14: TPQ1.B2, Part3.A1, R14.Pin_0
  N15: TPQ1.E3, Part3.A2, R15.Pin_0
  N16: TPQ1.E4, Part3.D12~/MISO, R11.Pin_1
  N17: Part3.RESET, Part3.A7, U3.ST_CP
  N18: Part3.D2, TPQ2.B2, R6.Pin_0
  N19: Part3.D3~, TPQ2.B1, R7.Pin_0
  N20: Part3.D4, S1.L1, R16.Pin_1, SELECT.pin3
  N21: Part3.D5~, TPQ2.B4, R8.Pin_1
  N22: Part3.D6~, TPQ2.B3, R9.Pin_1
  N23: Part3.D7, S1.L2, R5.Pin_1, SELECT.pin1
  N24: Part3.D8, >>.Pin_3, >>.Pin_4, >>_2.pin1, R23.Pin_1
  N25: Part3.D9~, <<.Pin_3, <<.Pin_4, <<_2.pin1, R24.Pin_1
  N26: Part3.A6, U3.SH_CP
  N27: Part3.A5, LC_I2C.pin1
  N28: Part3.A4, LC_I2C.pin2
  N29: TPQ2.E1, FUEL_2.pin6
  N30: TPQ2.E2, FUEL_2.pin7, FUEL_SAFE.pin1
  N31: TPQ2.E3, OX_2.pin7, OX_SAFE.pin1
  N32: TPQ2.E4, OX_2.pin6
  N33: R18.Pin_0, FUEL_2.pin8, FUEL_SAFE.pin2
  N34: LED1.cathode, R32.Pin_0
  N35: LED1.anode, U3.Q7
  N36: LED2.cathode, R31.Pin_0
  N37: LED2.anode, U3.Q6
  N38: LED3.cathode, R30.Pin_0
  N39: LED3.anode, U3.Q5
  N40: LED4.cathode, R29.Pin_0
  N41: LED4.anode, U3.Q4
  N42: LED5.cathode, R28.Pin_0
  N43: LED5.anode, U3.Q3
  N44: LED6.cathode, R27.Pin_0
  N45: LED6.anode, U3.Q2
  N46: LED7.cathode, R26.Pin_0
  N47: LED7.anode, U3.Q1
  N48: LED8.cathode, R25.Pin_0
  N49: LED8.anode, U3.Q0
  N50: OX_2.pin8, R33.Pin_0, OX_SAFE.pin2

custom parts:
  DIP - 14 pins: PNP Array
  Arduino Nano 33 IOT: The Arduino Nano 33 IoT is the easiest and cheapest point of entry to enhance existing devices (and creating new ones) to be part of the IoT and designing pico-network applications. Whether you are looking at building a sensor network connected to your office or home router, or if you want to create a BLE device sending data to a cellphone, the Nano 33 IoT is your one-stop-solution for many of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
