# Fritzing sketch Controller-Schematic-Rev_C (saved by Fritzing 0.9.10b)
breadboards: 2

parts:
  Part3 = Arduino Nano 33 IOT
  << = Pushbutton [package="[THT]"]
  >> = Pushbutton [package="[THT]"]
  S1 = Toggle Switch [package=THT]
  R5 = Resistor [tolerance=±5% power=0.25 resistance=4.7k package=THT]
  TPQ2 = DIP - 14 pins [chip_label=TPQ3906 package="DIP (Dual Inline) [THT]"]
  R7 = Resistor [tolerance=±5% power=0.25 resistance=4.7k package=THT]
  R8 = Resistor [tolerance=±5% power=0.25 resistance=4.7k package=THT]
  R9 = Resistor [tolerance=±5% power=0.25 resistance=4.7k package=THT]
  R6 = Resistor [tolerance=±5% power=0.25 resistance=4.7k package=THT]
  R11 = Resistor [tolerance=±5% power=0.25 resistance=4.7k package=THT]
  R10 = Resistor [tolerance=±5% power=0.25 resistance=4.7k package=THT]
  R14 = Resistor [tolerance=±5% power=0.25 resistance=4.7k package=THT]
  R15 = Resistor [tolerance=±5% power=0.25 resistance=4.7k package=THT]
  R16 = Resistor [tolerance=±5% power=0.25 resistance=4.7k package=THT]
  LC_I2C = Screw terminal - 2 pins [package=THT]
  R18 = Resistor [tolerance=±5% power=0.25 resistance=4.7k package=THT]
  >>_2 = male pin header, 2 pins [form="♂ (male)"]
  <<_2 = male pin header, 2 pins [form="♂ (male)"]
  R23 = Resistor [tolerance=±5% power=0.25 resistance=4.7k package=THT]
  R24 = Resistor [tolerance=±5% power=0.25 resistance=4.7k package=THT]
  LED1 = LED - 5mm [color="Red (633nm)" current=0.030 package="5 mm [THT]"]
  LED2 = LED - 5mm [color="Red (633nm)" current=0.030 package="5 mm [THT]"]
  LED3 = LED - 5mm [color="Red (633nm)" current=0.030 package="5 mm [THT]"]
  LED4 = LED - 5mm [color="Red (633nm)" current=0.030 package="5 mm [THT]"]
  LED5 = LED - 5mm [color="Red (633nm)" current=0.030 package="5 mm [THT]"]
  LED6 = LED - 5mm [color="Red (633nm)" current=0.030 package="5 mm [THT]"]
  LED7 = LED - 5mm [color="Red (633nm)" current=0.030 package="5 mm [THT]"]
  LED8 = LED - 5mm [color="Red (633nm)" current=30mA package="5 mm [THT]"]
  U3 = 74HC595 [package="DIP16 [THT]"]
  R25 = Resistor [tolerance=±5% power=0.25 resistance=470 package=THT]
  R26 = Resistor [tolerance=±5% power=0.25 resistance=470 package=THT]
  R27 = Resistor [tolerance=±5% power=0.25 resistance=470 package=THT]
  R28 = Resistor [tolerance=±5% power=0.25 resistance=470 package=THT]
  R29 = Resistor [tolerance=±5% power=0.25 resistance=470 package=THT]
  R30 = Resistor [tolerance=±5% power=0.25 resistance=470 package=THT]
  R31 = Resistor [tolerance=±5% power=0.25 resistance=470 package=THT]
  R32 = Resistor [tolerance=±5% power=0.25 resistance=470 package=THT]
  SELECT = male pin header, 3 pins [form="♂ (male)"]
  R33 = Resistor [tolerance=±5% power=0.25 resistance=4.7k package=THT]
  FUEL_SAFE = male pin header, 2 pins [form="♂ (male)"]
  OX_SAFE = male pin header, 2 pins [form="♂ (male)"]
  OX = male pin header, 7 pins [form="♂ (male)"]
  FUEL = male pin header, 7 pins [form="♂ (male)"]
  TPQ3 = DIP - 14 pins [chip_label=TPQ3906 package="DIP (Dual Inline) [THT]"]
  R34 = Resistor [tolerance=±5% power=0.25 resistance=4.7k package=THT]
  R35 = Resistor [tolerance=±5% power=0.25 resistance=4.7k package=THT]
  R36 = Resistor [tolerance=±5% power=0.25 resistance=4.7k package=THT]
  R37 = Resistor [tolerance=±5% power=0.25 resistance=4.7k package=THT]
  OX1 = IC, DIP package, 8 pins [chip_label=LTC1690]
  FUEL1 = IC, DIP package, 8 pins [chip_label=LTC1690]
  POWER_IN1 = Screw terminal - 2 pins [package=THT]
  LM1084-3_3V1 = Voltage Regulator - 3.3V [part_number=LM1084IT-3.3/NOPB package="TO220 [THT]"]
  C3 = Tantalum Capacitor [capacitance=10µF voltage=10V package="200 mil [THT, tantalum]"]
  C4 = Electrolytic Capacitor [capacitance=10µF voltage=16V part_number=ECA-1CM100I package="100 mil [THT, electrolytic]"]
  R38 = Resistor [tolerance=±5% power=0.25 resistance=4.7k package=THT]

nets:
  N1: Part3.RESET, Part3.A7
  GND: Part3.GND, Part3.D13~, R7.Pin_1, R8.Pin_0, R9.Pin_0, R6.Pin_1, R10.Pin_1, R14.Pin_1, R15.Pin_1, R18.Pin_1, U3.GND, U3.SH_CP, U3.OE, R25.Pin_1, R26.Pin_1, R27.Pin_1, R28.Pin_1, R29.Pin_1, R30.Pin_1, R31.Pin_1, R32.Pin_1, R33.Pin_1, OX.pin5, FUEL.pin5, TPQ3.B1, R34.Pin_1, R35.Pin_1, R36.Pin_1, R37.Pin_1, OX1.pin1, OX1.pin4, POWER_IN1.pin1, LM1084-3_3V1.GND, C3.-, C4.-
  N2: Part3.D2, >>.Pin_3, >>.Pin_4, >>_2.pin1, R23.Pin_1
  N3: Part3.D3~, TPQ2.B1, R7.Pin_0
  N4: Part3.D4, S1.L2, R5.Pin_1, SELECT.pin1
  N5: Part3.D5~, TPQ2.B4, R8.Pin_1
  N6: Part3.D6~, TPQ2.B3, R9.Pin_1
  N7: Part3.D7, TPQ2.B2, R6.Pin_0
  N8: Part3.D8, U3.ST_CP
  N9: Part3.D9~, <<.Pin_3, <<.Pin_4, <<_2.pin1, R24.Pin_1
  N10: Part3.D10~, S1.L1, R16.Pin_1, SELECT.pin3
  N11: Part3.D11/MOSI, Part3.+5V, U3.DS, R38.Pin_1
  N12: Part3.D12~/MISO, R11.Pin_1, TPQ3.E4
  N13: Part3.VIN, TPQ2.C1, TPQ2.C2, TPQ2.C3, TPQ2.C4, R10.Pin_0, TPQ3.C1, TPQ3.C2, FUEL1.pin1, POWER_IN1.pin2, LM1084-3_3V1.input_voltage, C4.+
  N14: Part3.A5, LC_I2C.pin1
  N15: Part3.A4, LC_I2C.pin2
  N16: Part3.A2, R15.Pin_0
  N17: Part3.A1, R14.Pin_0, TPQ3.B2
  N18: <<.Pin_1, <<.Pin_2, >>.Pin_1, >>.Pin_2, R5.Pin_0, R16.Pin_0, >>_2.pin2, <<_2.pin2
  N19: S1.COM, R11.Pin_0, R23.Pin_0, R24.Pin_0, U3.MR, U3.VCC, SELECT.pin2, TPQ3.C3, TPQ3.C4, LM1084-3_3V1.output_voltage, C3.+, R38.Pin_0
  N20: TPQ2.E1, FUEL.pin6
  N21: TPQ2.E2, FUEL_SAFE.pin1, FUEL.pin7
  N22: TPQ2.E3, OX_SAFE.pin1, OX.pin7
  N23: TPQ2.E4, OX.pin6
  N24: R18.Pin_0, FUEL_SAFE.pin2
  N25: LED1.cathode, R32.Pin_0
  N26: LED1.anode, U3.Q7
  N27: LED2.cathode, R31.Pin_0
  N28: LED2.anode, U3.Q6
  N29: LED3.cathode, R30.Pin_0
  N30: LED3.anode, U3.Q5
  N31: LED4.cathode, R29.Pin_0
  N32: LED4.anode, U3.Q4
  N33: LED5.cathode, R28.Pin_0
  N34: LED5.anode, U3.Q3
  N35: LED6.cathode, R27.Pin_0
  N36: LED6.anode, U3.Q2
  N37: LED7.cathode, R26.Pin_0
  N38: LED7.anode, U3.Q1
  N39: LED8.cathode, R25.Pin_0
  N40: LED8.anode, U3.Q0
  N41: R33.Pin_0, OX_SAFE.pin2
  N42: OX.pin1, OX1.pin8
  N43: OX.pin2, OX1.pin7
  N44: OX.pin3, OX1.pin6
  N45: OX.pin4, OX1.pin5
  N46: FUEL.pin1, FUEL1.pin8
  N47: FUEL.pin2, FUEL1.pin7
  N48: FUEL.pin3, FUEL1.pin6
  N49: FUEL.pin4, FUEL1.pin5
  N50: TPQ3.E1, R35.Pin_0, FUEL1.pin3
  N51: TPQ3.E2, R36.Pin_0, OX1.pin3
  N52: TPQ3.B3, R34.Pin_0, OX1.pin2
  N53: TPQ3.B4, R37.Pin_0, FUEL1.pin2

custom parts:
  Arduino Nano 33 IOT: The Arduino Nano 33 IoT is the easiest and cheapest point of entry to enhance existing devices (and creating new ones) to be part of the IoT and designing pico-network applications. Whether you are looking at building a sensor network connected to your office or home router, or if you want to create a BLE device sending data to a cellphone, the Nano 33 IoT is your one-stop-solution for many of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
  DIP - 14 pins: PNP Array
