# Fritzing sketch Controller-Schematic-Rev_E (saved by Fritzing 0.9.10b)
breadboards: 3

parts:
  Part3 = Arduino Nano 33 IOT
  LM1084-3_3V1 = Voltage Regulator - 3.3V [part_number=LM1084IT-3.3/NOPB package="TO220 [THT]"]
  C2 = Tantalum Capacitor [capacitance=10µF voltage=15V part_number=CWR11HH106KB package="200 mil [THT, tantalum]"]
  C1 = Electrolytic Capacitor [capacitance=10µF voltage=10V part_number=C1210C106J8NAC7800 package="100 mil [THT, electrolytic]"]
  OX = DB9 Connector [part_number="A-DF 09 A/KG-T2S" package=db9]
  FUEL = DB9 Connector [part_number="A-DF 09 A/KG-T2S" package=db9]
  FUEL_2 = IC, DIP package, 8 pins [chip_label=LTC1690 part_number=LTC1690CN8#PBF]
  OX_2 = IC, DIP package, 8 pins [chip_label=LTC1690 part_number=LTC1690CN8#PBF]
  EXT = IC, DIP package, 8 pins [chip_label=LTC1690 part_number=LTC1690CN8#PBF]
  FUEL-ISO = SO16 [chip_label=ISO7740 part_number=ISO7740FQDWQ1 package=SO]
  OX-ISO = SO16 [chip_label=ISO7740 part_number=ISO7740FQDWQ1 package=SO]
  SER_EN = single row smd female pin header, 2 pins [form="♀ (female)"]
  EXT_2 = DB9 Connector [part_number="A-DF 09 A/KG-T2S" package=db9]
  74AHC597 = 74HC595 [part_number=SN74AHC595N package="DIP16 [THT]"]
  74AHC598 = 74HC595 [part_number=SN74AHC595N package="DIP16 [THT]"]
  SN74LXCH8 = QFN-24 [chip_label=SN74LXCH8 part_number=SN74LXCH8T245RHLR package=QFN]
  C3 = Electrolytic Capacitor [capacitance=0.1µF voltage=16V part_number=C1206X104G4HAC7800 package="100 mil [THT, electrolytic]"]
  C4 = Electrolytic Capacitor [capacitance=1µF voltage=10V part_number=C0805C105J8NAC7800 package="100 mil [THT, electrolytic]"]
  C5 = Electrolytic Capacitor [capacitance=0.1µF voltage=16V part_number=C1206X104G4HAC7800 package="100 mil [THT, electrolytic]"]
  C6 = Electrolytic Capacitor [capacitance=1µF voltage=10V part_number=C0805C105J8NAC7800 package="100 mil [THT, electrolytic]"]
  C7 = Electrolytic Capacitor [capacitance=0.1µF voltage=16V part_number=C1206X104G4HAC7800 package="100 mil [THT, electrolytic]"]
  C8 = Electrolytic Capacitor [capacitance=1µF voltage=10V part_number=C0805C105J8NAC7800 package="100 mil [THT, electrolytic]"]
  C9 = Electrolytic Capacitor [capacitance=0.1µF voltage=16V part_number=C1206X104G4HAC7800 package="100 mil [THT, electrolytic]"]
  C10 = Electrolytic Capacitor [capacitance=1µF voltage=10V part_number=C0805C105J8NAC7800 package="100 mil [THT, electrolytic]"]
  C11 = Electrolytic Capacitor [capacitance=0.1µF voltage=16V part_number=C1206X104G4HAC7800 package="100 mil [THT, electrolytic]"]
  C12 = Electrolytic Capacitor [capacitance=1µF voltage=10V part_number=C0805C105J8NAC7800 package="100 mil [THT, electrolytic]"]
  C13 = Electrolytic Capacitor [capacitance=0.1µF voltage=16V part_number=C1206X104G4HAC7800 package="100 mil [THT, electrolytic]"]
  C14 = Electrolytic Capacitor [capacitance=1µF voltage=10V part_number=C0805C105J8NAC7800 package="100 mil [THT, electrolytic]"]
  C15 = Electrolytic Capacitor [capacitance=0.1µF voltage=16V part_number=C1206X104G4HAC7800 package="100 mil [THT, electrolytic]"]
  C16 = Electrolytic Capacitor [capacitance=1µF voltage=10V part_number=C0805C105J8NAC7800 package="100 mil [THT, electrolytic]"]
  C17 = Electrolytic Capacitor [capacitance=0.1µF voltage=16V part_number=C1206X104G4HAC7800 package="100 mil [THT, electrolytic]"]
  C18 = Electrolytic Capacitor [capacitance=1µF voltage=10V part_number=C0805C105J8NAC7800 package="100 mil [THT, electrolytic]"]
  C19 = Electrolytic Capacitor [capacitance=0.1µF voltage=16V part_number=C1206X104G4HAC7800 package="100 mil [THT, electrolytic]"]
  C20 = Electrolytic Capacitor [capacitance=1µF voltage=10V part_number=C0805C105J8NAC7800 package="100 mil [THT, electrolytic]"]
  C21 = Electrolytic Capacitor [capacitance=0.1µF voltage=16V part_number=C1206X104G4HAC7800 package="100 mil [THT, electrolytic]"]
  C22 = Electrolytic Capacitor [capacitance=1µF voltage=10V part_number=C0805C105J8NAC7800 package="100 mil [THT, electrolytic]"]
  C23 = Electrolytic Capacitor [capacitance=0.1µF voltage=16V part_number=C1206X104G4HAC7800 package="100 mil [THT, electrolytic]"]
  C24 = Electrolytic Capacitor [capacitance=1µF voltage=10V part_number=C0805C105J8NAC7800 package="100 mil [THT, electrolytic]"]
  C25 = Electrolytic Capacitor [capacitance=0.1µF voltage=16V part_number=C1206X104G4HAC7800 package="100 mil [THT, electrolytic]"]
  C26 = Electrolytic Capacitor [capacitance=1µF voltage=10V part_number=C0805C105J8NAC7800 package="100 mil [THT, electrolytic]"]
  R1 = Resistor [tolerance=±5% power=0.25 resistance=130 part_number=RC0100JR-07130RL package=THT]
  R2 = Resistor [tolerance=±5% power=0.25 resistance=130 part_number=RC0100JR-07130RL package=THT]
  R3 = Resistor [tolerance=±5% power=0.25 resistance=130 part_number=RC0100JR-07130RL package=THT]
  R4 = Resistor [tolerance=±5% power=0.25 resistance=130 part_number=RC0100JR-07130RL package=THT]
  R5 = Resistor [tolerance=±5% power=0.25 resistance=130 part_number=RC0100JR-07130RL package=THT]
  R6 = Resistor [tolerance=±5% power=0.25 resistance=130 part_number=RC0100JR-07130RL package=THT]
  R7 = Resistor [tolerance=±5% power=0.25 resistance=130 part_number=RC0100JR-07130RL package=THT]
  R8 = Resistor [tolerance=±5% power=0.25 resistance=300 part_number=PFR02S-301-FNH package=THT]
  R9 = Resistor [tolerance=±5% power=0.25 resistance=130 part_number=RC0100JR-07130RL package=THT]
  R10 = Resistor [tolerance=±5% power=0.25 resistance=130 part_number=RC0100JR-07130RL package=THT]
  R11 = Resistor [tolerance=±5% power=0.25 resistance=130 part_number=RC0100JR-07130RL package=THT]
  R12 = Resistor [tolerance=±5% power=0.25 resistance=130 part_number=RC0100JR-07130RL package=THT]
  R13 = Resistor [tolerance=±5% power=0.25 resistance=130 part_number=RC0100JR-07130RL package=THT]
  R14 = Resistor [tolerance=±5% power=0.25 resistance=130 part_number=RC0100JR-07130RL package=THT]
  R15 = Resistor [tolerance=±5% power=0.25 resistance=130 part_number=RC0100JR-07130RL package=THT]
  R16 = Resistor [tolerance=±5% power=0.25 resistance=130 part_number=RC0100JR-07130RL package=THT]
  XGURU_GREEN_ANODE = male pin header, 8 pins [form="♂ (male)" part_number=XGURUGX10D]
  XGURU_RED_ANODE = male pin header, 8 pins [form="♂ (male)" part_number=XGURUGX10D]
  XGURU_CATHODE = male pin header, 8 pins [form="♂ (male)" part_number=XGURUGX10D]

nets:
  N1: Part3.RX, EXT.pin3
  N2: Part3.TX, SN74LXCH8.5
  N3: Part3.RESET, Part3.A7, SN74LXCH8.6
  GND: Part3.GND, Part3.D13~, LM1084-3_3V1.GND, C2.-, C1.-, FUEL_2.pin3, FUEL_2.pin4, OX_2.pin4, EXT.pin4, SER_EN.pin1, EXT_2.5, 74AHC597.GND, 74AHC597.OE, 74AHC598.GND, 74AHC598.SH_CP, 74AHC598.OE, SN74LXCH8.2, SN74LXCH8.11, SN74LXCH8.12, SN74LXCH8.13, SN74LXCH8.22, C3.-, C4.-, C5.-, C6.-, C7.-, C8.-, C9.-, C10.-, C11.-, C12.-, C13.-, C14.-, C17.-, C18.-, XGURU_CATHODE.pin1, XGURU_CATHODE.pin2, XGURU_CATHODE.pin3, XGURU_CATHODE.pin4, XGURU_CATHODE.pin5, XGURU_CATHODE.pin6, XGURU_CATHODE.pin7, XGURU_CATHODE.pin8
  N4: Part3.D2, SN74LXCH8.8
  N5: Part3.D3~, SER_EN.pin2
  N6: Part3.D4, SN74LXCH8.4
  N7: Part3.D5~, OX_2.pin3, 74AHC597.SH_CP
  N8: Part3.D6~, 74AHC597.DS
  N9: Part3.D7, 74AHC597.ST_CP
  N10: Part3.D8, 74AHC598.ST_CP
  N11: Part3.D9~, OX-ISO.4
  N12: Part3.D10~, FUEL-ISO.4
  N13: Part3.D11/MOSI, Part3.+5V, 74AHC598.DS
  N14: Part3.D12~/MISO, SN74LXCH8.3
  N15: Part3.VIN, LM1084-3_3V1.output_voltage, C2.+, FUEL-ISO.1, OX-ISO.1, SN74LXCH8.1, C3.+, C4.+, C7.+, C8.+, C15.+, C16.+, C17.+, C18.+, C21.+, C22.+, C25.+, C26.+
  N16: Part3.A6, SN74LXCH8.7
  N17: Part3.A3, FUEL-ISO.3
  N18: Part3.A2, OX-ISO.3
  N19: Part3.A1, FUEL-ISO.5
  N20: Part3.A0, OX-ISO.5
  N21: Part3.3V3, R7.Pin_0
  N22: LM1084-3_3V1.input_voltage, C1.+, FUEL_2.pin1, OX_2.pin1, EXT.pin1, EXT_2.6, SN74LXCH8.23, SN74LXCH8.24, C5.+, C6.+, C9.+, C10.+, C11.+, C12.+, C13.+, C14.+, R8.Pin_0
  N23: OX.1, OX_2.pin8
  N24: OX.2, OX_2.pin7
  N25: OX.3, OX_2.pin6
  N26: OX.4, OX_2.pin5
  N27: OX.5, OX-ISO.10, OX-ISO.16, C23.+, C24.+
  N28: OX.6, OX-ISO.9, OX-ISO.15, C23.-, C24.-
  N29: OX.7, OX-ISO.14
  N30: OX.8, OX-ISO.13
  N31: OX.9, OX-ISO.12
  N32: FUEL.1, FUEL_2.pin8
  N33: FUEL.2, FUEL_2.pin7
  N34: FUEL.3, FUEL_2.pin6
  N35: FUEL.4, FUEL_2.pin5
  N36: FUEL.5, FUEL-ISO.10, FUEL-ISO.16, C19.+, C20.+
  N37: FUEL.6, FUEL-ISO.9, FUEL-ISO.15, C19.-, C20.-
  N38: FUEL.7, FUEL-ISO.14
  N39: FUEL.8, FUEL-ISO.13
  N40: FUEL.9, FUEL-ISO.12
  N41: FUEL_2.pin2, SN74LXCH8.21
  N42: OX_2.pin2, SN74LXCH8.20
  N43: EXT.pin2, SN74LXCH8.19
  N44: EXT.pin5, EXT_2.4
  N45: EXT.pin6, EXT_2.3
  N46: EXT.pin7, EXT_2.2
  N47: EXT.pin8, EXT_2.1
  N48: FUEL-ISO.2, FUEL-ISO.8, OX-ISO.2, OX-ISO.8, C15.-, C16.-, C21.-, C22.-, C25.-, C26.-
  N49: EXT_2.7, SN74LXCH8.16
  N50: EXT_2.8, SN74LXCH8.17
  N51: EXT_2.9, SN74LXCH8.18
  N52: 74AHC597.Q1, R14.Pin_0
  N53: 74AHC597.Q2, R12.Pin_0
  N54: 74AHC597.Q3, R13.Pin_0
  N55: 74AHC597.Q4, R10.Pin_0
  N56: 74AHC597.Q5, R11.Pin_0
  N57: 74AHC597.Q6, R15.Pin_0
  N58: 74AHC597.Q7, R16.Pin_0
  VCC: 74AHC597.MR, 74AHC597.VCC, 74AHC598.MR, 74AHC598.VCC
  N59: 74AHC597.Q0, R9.Pin_0
  N60: 74AHC598.Q1, R2.Pin_0
  N61: 74AHC598.Q2, R3.Pin_0
  N62: 74AHC598.Q3, R4.Pin_0
  N63: 74AHC598.Q4, R6.Pin_0
  N64: 74AHC598.Q5, R5.Pin_0
  N65: 74AHC598.Q0, R1.Pin_0
  N66: R1.Pin_1, XGURU_GREEN_ANODE.pin1
  N67: R2.Pin_1, XGURU_GREEN_ANODE.pin2
  N68: R3.Pin_1, XGURU_GREEN_ANODE.pin3
  N69: R4.Pin_1, XGURU_GREEN_ANODE.pin4
  N70: R5.Pin_1, XGURU_GREEN_ANODE.pin6
  N71: R6.Pin_1, XGURU_GREEN_ANODE.pin5
  N72: R7.Pin_1, XGURU_GREEN_ANODE.pin7
  N73: R8.Pin_1, XGURU_GREEN_ANODE.pin8
  N74: R9.Pin_1, XGURU_RED_ANODE.pin1
  N75: R10.Pin_1, XGURU_RED_ANODE.pin5
  N76: R11.Pin_1, XGURU_RED_ANODE.pin6
  N77: R12.Pin_1, XGURU_RED_ANODE.pin3
  N78: R13.Pin_1, XGURU_RED_ANODE.pin4
  N79: R14.Pin_1, XGURU_RED_ANODE.pin2
  N80: R15.Pin_1, XGURU_RED_ANODE.pin7
  N81: R16.Pin_1, XGURU_RED_ANODE.pin8

notes:
  Differences between Fritzing info and actual:
  >ISO 7740s are SOIC-16, not SO-16
  >Capacitor sizes (NOT what is listed in Fritzing spec):
  -CWR11HH106KB (10uF Tantalum): 2312
  -C1210C106J8NAC7800 (10uF electrolytic): 1210
  -C1206X104G4HAC7800 (.1uF): 1206
  -C0805C105J8NAC7800 (1uF): 0805
  >74HC595s are actually 74AHC595s
  >ISO7740s are SOIC-16 no SO16
  >SN74LXCH8s are VFQN-14, not QFN-24
  >XGURUGX10D anodes are actually DIP16 spaced, and the common cathode is in between them. Reference datasheet for spacing.
  >DB9 connectors are right-angle, not out of the face of the board
  > LED Resistors (RC0100JR-07130RL and PFR02S-301-FNH) are SMD size 01005, not THT
  > SER_EN "SMD header" is actually just 2 solder pads

custom parts:
  Arduino Nano 33 IOT: The Arduino Nano 33 IoT is the easiest and cheapest point of entry to enhance existing devices (and creating new ones) to be part of the IoT and designing pico-network applications. Whether you are looking at building a sensor network connected to your office or home router, or if you want to create a BLE device sending data to a cellphone, the Nano 33 IoT is your one-stop-solution for many of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
